# Fritzing sketch schematic (saved by Fritzing 0.9.10b)

parts:
  doit_esp32_devkit_v1 = DOIT Esp32 DevKit v1 (30 pins long, 11 pins width) [part_number=ESP32S-PIN30]
  Bauteil1 = LCD1602-I2C
  WriteMode = Toggle Switch [package=THT]
  U1 = POT [knob_status=50% power=0.5W package=pot_mammoth]
  RS485_module1 = RS485 Module (MAX3485)
  LED1 = LEDs [package=led10mm]
  Power = Toggle Switch [package=THT]
  Battery_/_Power_Source = Battery Holders [package=battery-aa]
  DMX-IN_(Male) = XLR NC3MAAH [package=nc3maah]
  DMX-OUT_(Female) = XLR3_NCFAH2 [package=xlr3_nc3fah2]

nets:
  N1: doit_esp32_devkit_v1.3V3, U1.E
  GND: doit_esp32_devkit_v1.GND, Bauteil1.GND, WriteMode.COM, U1.A, RS485_module1.GND, LED1.C, Battery_/_Power_Source.-, DMX-IN_(Male).2, DMX-OUT_(Female).2
  N2: doit_esp32_devkit_v1.D2, WriteMode.L2
  N3: doit_esp32_devkit_v1.RX2, RS485_module1.RO
  N4: doit_esp32_devkit_v1.TX2, RS485_module1.DI
  N5: doit_esp32_devkit_v1.D21, RS485_module1.RE, RS485_module1.DE
  N6: doit_esp32_devkit_v1.TX0, Bauteil1.SDA
  N7: doit_esp32_devkit_v1.D22, Bauteil1.SCL
  N8: doit_esp32_devkit_v1.VP, U1.S
  VCC: doit_esp32_devkit_v1.VIN, Bauteil1.VCC, RS485_module1.VCC, LED1.A, Power.L1
  N9: RS485_module1.A, DMX-IN_(Male).3, DMX-OUT_(Female).3
  N10: RS485_module1.B, DMX-IN_(Male).1, DMX-OUT_(Female).1
  N11: Power.COM, Battery_/_Power_Source.+
  N12: DMX-IN_(Male).G, DMX-OUT_(Female).G

notes:
  DMX/XLR Pins: For wiring, the connector numbers should be used
  Use the wiring diagramm for the XLR/DMX Ports.

custom parts:
  DOIT Esp32 DevKit v1 (30 pins long, 11 pins width): The DOIT Esp32 DevKit v1 is one of the development board created by DOIT to evaluate the ESP-WROOM-32 module. It is based on the ESP32 microcontroller that boasts Wifi, Bluetooth, Ethernet and Low Power support all in a single chip. (vanepp) made breadboard work, adjusted pin numbering and labels and reduced size of schematic and cleaned up pcb. This chip is 30pins long (2 x15) and 11 pins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
  LCD1602-I2C: A standard character display, usually with 2x16 characters. Comes in many colors with LCM1602 IIC attached.
  RS485 Module (MAX3485): Commercially available RS485 to RS232 TTL Module
